# Fritzing sketch Basic_esp_and_3v (saved by Fritzing 0.9.2b)
breadboards: 1

parts:
  LED1 = LED - 5mm [color="Red (633nm)" package="5 mm [THT]"]
  C1 = Electrolytic Capacitor [capacitance=1µF package="100 mil [THT, electrolytic]"]
  VCC1 = Battery
  VCC2 = Battery
  IC2 = Voltage Regulator - Variable [package="TO220 [THT]"]
  J1 = female pin header, 4 pins [form="♀ (female)"]
  J2 = female pin header, 4 pins [form="♀ (female)"]
  R3 = Resistor [tolerance=±5% resistance=33 package=THT]
  R1 = Resistor [tolerance=±5% resistance=100 package=THT]
  Part1 = FTDI Basic Programmer

nets:
  N1: LED1.cathode, C1.-, VCC1.-, IC2.ADJ, J1.pin4, Part1.GND
  N2: LED1.anode, R1.Pin_0
  N3: C1.+, IC2.OUT, J2.pin1, R3.Pin_1, R1.Pin_1
  N4: VCC1.+, VCC2.-
  N5: VCC2.+, IC2.IN
  N6: J1.pin1, Part1.RXI
  N7: J2.pin3, R3.Pin_0
  N8: J2.pin4, Part1.TXO

notes:
  Use batteries or FTDI VCC - but NOT both
