# Fritzing sketch RemoteLedControl (saved by Fritzing 0.9.2b)
breadboards: 1

parts:
  LED1 = LED - 5mm [color="Red (633nm)" package="5 mm [THT]"]
  C1 = Electrolytic Capacitor [capacitance=3.3µF package="100 mil [THT, electrolytic]"]
  VCC1 = Battery
  VCC2 = Battery
  J1 = female pin header, 4 pins [form="♀ (female)"]
  J2 = female pin header, 4 pins [form="♀ (female)"]
  J4 = female pin header, 6 pins [form="♀ (female)"]
  LED2 = LED - 5mm [color="Green (570nm)" package="5 mm [THT]"]
  R3 = Resistor [tolerance=±5% resistance=10k package=THT]
  R1 = Resistor [tolerance=±5% resistance=100 package=THT]
  R2 = Resistor [tolerance=±5% resistance=100 package=THT]
  IC2 = Voltage Regulator - Variable [part_number=LD33V package="TO220 [THT]"]

nets:
  N1: LED1.cathode, C1.-, VCC1.-, J1.pin4, J4.pin6, R2.Pin_0, IC2.ADJ
  N2: LED1.anode, R1.Pin_0
  N3: C1.+, J2.pin1, R3.Pin_1, R1.Pin_1, IC2.OUT
  N4: VCC1.+, VCC2.-
  N5: VCC2.+, J4.pin4, IC2.IN
  N6: J1.pin1, J4.pin3
  N7: J1.pin2, LED2.anode
  N8: J2.pin3, R3.Pin_0
  N9: J2.pin4, J4.pin2
  N10: LED2.cathode, R2.Pin_1

notes:
  serial cable
  +3.3v
  gnd
  cts
  vcc
  txd
  rxd
  rts
  6v
  R1
  R2
  R3
