# Fritzing sketch RemoteLedControlMin (saved by Fritzing 0.9.2b)
circuit board: 4.98572cm x 5.5302cm
breadboards: 1

parts:
  BAT1 = Battery Holders [package=battery_20mm_pth_compact]
  BAT2 = Battery Holders [package=battery_20mm_pth_compact]
  LED3 = smd LED [color="Green (570nm)" package="1206 [SMD]"]
  R5 = Resistor [tolerance=±5% resistance=100 package="1206 [SMD]"]
  J7 = single row smd female pin header, 3 pins [form="♀ (female)"]
  J5 = double row smd female pin header, 8 pins [form="♀ (female)"]
  R4 = Resistor [tolerance=±5% resistance=33 package="1206 [SMD]"]

nets:
  N1: BAT1.+, J5.pin8, R4.Pin_0
  N2: BAT1.-, BAT2.+
  N3: BAT2.-, R5.Pin_0, J7.pin1, J5.pin1
  N4: LED3.cathode, R5.Pin_1
  N5: LED3.anode, J5.pin3
  N6: J7.pin2, J5.pin5
  N7: J7.pin3, J5.pin4
  N8: J5.pin6, R4.Pin_1

notes:
  tx
  rx
  gpio0(3)
  gpio2
  gnd
  vcc
  ch_pd
