# Fritzing sketch esp_3v_usb (saved by Fritzing 0.9.2b)
breadboards: 1

parts:
  LED1 = LED - 5mm [color="Red (633nm)" package="5 mm [THT]"]
  C1 = Electrolytic Capacitor [capacitance=10µF package="100 mil [THT, electrolytic]"]
  IC2 = Voltage Regulator - Variable [package="TO220 [THT]"]
  J1 = female pin header, 4 pins [form="♀ (female)"]
  J2 = female pin header, 4 pins [form="♀ (female)"]
  R3 = Resistor [tolerance=±5% resistance=330 package=THT]
  R1 = Resistor [tolerance=±5% resistance=100 package=THT]
  Part1 = FTDI Basic Programmer
  U1 = ESP8266 WiFi Module [part_number=ESP8266]

nets:
  GND: LED1.cathode, C1.-, IC2.ADJ, J1.pin4, Part1.GND, U1.GND
  N1: LED1.anode, R1.Pin_0
  N2: C1.+, IC2.OUT, J2.pin1, R3.Pin_1, R1.Pin_1, U1.VCC
  N3: IC2.IN, Part1.POWER
  N4: J1.pin1, Part1.TXO, U1.RXD
  N5: J1.pin2, U1.GPIO_0
  N6: J1.pin3, U1.GPIO_2
  N7: J2.pin2, U1.RST
  N8: J2.pin3, R3.Pin_0, U1.CH_PD
  N9: J2.pin4, Part1.RXI, U1.TXD

custom parts:
  ESP8266 WiFi Module: Generic WiFi Module based on the ESP8266 with onboard PCB antenna and UART communications
