# Fritzing sketch led-strip-servo-motor-attempt (saved by Fritzing 0.9.3b)
breadboards: 1

parts:
  U1 = NodeMCU V3.0
  LPD8806_RGB_LED_Strip1 = LPD8806 RGB LED Strip
  J1 = Basic Servo
  R1 = Resistor [tolerance=±5% resistance=220 package=THT]
  Q1 = NPN-Transistor [package="TO92 [THT]"]
  J2 = Basic Servo
  R2 = Resistor [tolerance=±5% resistance=1k package=THT]

nets:
  N1: U1.D1, LPD8806_RGB_LED_Strip1.DI
  N2: U1.D2, LPD8806_RGB_LED_Strip1.CI
  N3: U1.VU, LPD8806_RGB_LED_Strip1.+5V#3, J1.vcc
  GND: U1.GND, LPD8806_RGB_LED_Strip1.GND#0, J1.gnd
  N4: LPD8806_RGB_LED_Strip1.GND#4, J2.gnd
  N5: LPD8806_RGB_LED_Strip1.+5V#7, J2.vcc, R2.Pin_0
  N6: R1.Pin_1, Q1.B
  N7: Q1.C, J2.pulse, R2.Pin_1

notes:
  Servo attached to LED cathode
  Doesn't work - voltage change too low
  Servo attached via NPN transistor
  Frequencies not compatible

custom parts:
  NodeMCU V3.0: ESP8266 based NodeMCU
  LPD8806 RGB LED Strip: Digitally addressable RGB LED strip
