# Fritzing sketch esp-analog-thumb-stick (saved by Fritzing 0.9.3b)
breadboards: 1

parts:
  Part1 = Thumb Joystick
  VCC1 = Battery
  R1 = Resistor [tolerance=±5% resistance=2.2k package=THT]
  Q1 = NPN-Transistor [package="TO92 [THT]"]
  R2 = Resistor [tolerance=±5% resistance=2.2k package=THT]
  Q2 = NPN-Transistor [package="TO92 [THT]"]

nets:
  GND: Part1.GND, VCC1.-
  Button: Part1.SEL
  N1: Part1.HORZ, Q1.C
  N2: Part1.VERT, Q2.C
  3.3V: Part1.VCC, VCC1.+
  N3: R1.Pin_0, Q1.B
  read x: R1.Pin_1
  analog out: Q1.E, Q2.E
  N4: R2.Pin_0, Q2.B
  read y: R2.Pin_1

notes:
  To Analog 0>
  <From Digital A<
  <From Digital B<
